// Logisim project one instruction cpu.circ as structural Verilog
module main (
);

  wire alu_1_leq_zero, Bootlaoder_unlock_system, Bootlaoder_write_ram, button_1_out, clock_1_out,
       decoder_1_save_result, decoder_1_value_1, decoder_1_value_2, not_1_out, or_1_out, pc_1_new_instruction;
  wire [1:0] decoder_1_mem_addr;
  wire [15:0] adder_1_out, alu_1_out_6, Bootlaoder_address, Bootlaoder_data, counter_1_q, decoder_1_out_5,
       memory_1_data_out, multiplexer_1_out, multiplexer_2_out, multiplexer_3_out, pc_1_counter,
       register_1_q, sub_instruction_counter_1_sub_address;

  Counter #(.width(16), .max('hffff)) counter_1 (
    .load(1'b0), .count(1'b1), .Q(counter_1_q), .clk(clock_1_out), .clr(button_1_out));  // open: D, carry
  Clock clock_1 (.out(clock_1_out));
  Button button_1 (.out(button_1_out));
  Hex_Digit_Display hex_digit_display_1 (.value(counter_1_q[15:12]));  // open: dp
  Hex_Digit_Display hex_digit_display_2 (.value(counter_1_q[11:8]));  // open: dp
  Hex_Digit_Display hex_digit_display_3 (.value(counter_1_q[3:0]));  // open: dp
  Hex_Digit_Display hex_digit_display_4 (.value(counter_1_q[7:4]));  // open: dp
  pc pc_1 (
    .address(decoder_1_out_5), .jump(alu_1_leq_zero), .clock(clock_1_out), .reset(button_1_out),
    .lock(not_1_out), .Counter(pc_1_counter), .New_instruction(pc_1_new_instruction));
  sub_instruction_counter sub_instruction_counter_1 (
    .new_instruction(pc_1_new_instruction), .clock(clock_1_out), .clear(button_1_out), .lock(not_1_out),
    .sub_address(sub_instruction_counter_1_sub_address));
  Adder #(.width(16)) adder_1 (
    .a(pc_1_counter), .b(sub_instruction_counter_1_sub_address), .out(adder_1_out));  // open: cin, cout
  decoder decoder_1 (
    .data(memory_1_data_out), .sub_instruction(sub_instruction_counter_1_sub_address), .clock(clock_1_out),
    .reset(button_1_out), .out_5(decoder_1_out_5), .mem_addr(decoder_1_mem_addr),
    .save_result(decoder_1_save_result), .value_1(decoder_1_value_1), .value_2(decoder_1_value_2));
  Register #(.width(16)) register_1 (
    .D(memory_1_data_out), .Q(register_1_q), .clk(clock_1_out), .clr(button_1_out));  // open: en
  not not_1 (not_1_out, Bootlaoder_unlock_system);
  Multiplexer #(.select(2), .width(16), .enable("false")) multiplexer_1 (
    .in0(adder_1_out), .in1(decoder_1_out_5), .in3(register_1_q), .out(multiplexer_1_out),
    .sel(decoder_1_mem_addr));  // open: in2
  Multiplexer #(.width(16), .enable("false")) multiplexer_2 (
    .in0(Bootlaoder_address), .in1(multiplexer_1_out), .out(multiplexer_2_out), .sel(Bootlaoder_unlock_system));
  bootloader Bootlaoder (
    .clock(clock_1_out), .reset(button_1_out), .Address(Bootlaoder_address), .Data(Bootlaoder_data),
    .Write_ram(Bootlaoder_write_ram), .unlock_system(Bootlaoder_unlock_system));
  Multiplexer #(.width(16), .enable("false")) multiplexer_3 (
    .in0(Bootlaoder_data), .in1(alu_1_out_6), .out(multiplexer_3_out), .sel(Bootlaoder_unlock_system));
  or or_1 (or_1_out, decoder_1_save_result, Bootlaoder_write_ram);
  memory memory_1 (
    .address(multiplexer_2_out), .clock(clock_1_out), .write_nread(or_1_out), .reset(button_1_out),
    .data_in(multiplexer_3_out), .data_out(memory_1_data_out));
  alu alu_1 (
    .in_1(memory_1_data_out), .value_1(decoder_1_value_1), .value_2(decoder_1_value_2), .clock(clock_1_out),
    .reset(button_1_out), .out_6(alu_1_out_6), .LEQ_zero(alu_1_leq_zero));
endmodule

module clock_divider (
  input  clock_in,
  input  [15:0] divide_by,
  input  reset,
  input  lock,
  output clock_out
);

  wire [15:0] adder_1_out, multiplexer_1_out, multiplexer_2_out, register_1_q;

  Multiplexer #(.width(16), .enable("false")) multiplexer_1 (
    .in0(multiplexer_2_out), .in1({16{1'b0}}), .out(multiplexer_1_out), .sel(lock));
  Register #(.width(16)) register_1 (.D(multiplexer_1_out), .Q(register_1_q), .clk(clock_in), .clr(reset));  // open: en
  Adder #(.width(16)) adder_1 (.a(register_1_q), .b(16'h1), .out(adder_1_out));  // open: cin, cout
  Multiplexer #(.width(16), .enable("false")) multiplexer_2 (
    .in0(adder_1_out), .in1(16'h1), .out(multiplexer_2_out), .sel(clock_out));
  Comparator #(.width(16)) comparator_1 (.a(register_1_q), .b(divide_by), .eq(clock_out));  // open: gt, lt
endmodule

// PC
module pc (
  input  [15:0] address,
  input  jump,
  input  clock,
  input  reset,
  input  lock,
  output [15:0] Counter,
  output New_instruction
);

  wire [15:0] adder_1_out, multiplexer_1_out;

  Multiplexer #(.width(16), .enable("false")) multiplexer_1 (
    .in0(adder_1_out), .in1(address), .out(multiplexer_1_out), .sel(jump));
  Register #(.width(16)) register_1 (
    .D(multiplexer_1_out), .Q(Counter), .clk(New_instruction), .clr(reset));  // open: en
  clock_divider clock_divider_1 (
    .clock_in(clock), .divide_by(16'h8), .reset(reset), .lock(lock), .clock_out(New_instruction));
  Adder #(.width(16)) adder_1 (.a(Counter), .b(16'h3), .out(adder_1_out));  // open: cin, cout

  // Notes on the sheet:
  //   stages
  //   instruction size
endmodule

// RAM
module memory (
  input  [15:0] address,
  input  clock,
  input  write_nread,
  input  reset,
  input  [15:0] data_in,
  output [15:0] data_out
);

  wire not_1_out;
  wire [15:0] multiplexer_1_out, undriven;

  not not_1 (not_1_out, write_nread);
  RAM #(.addrWidth(16), .dataWidth(16)) ram_1 (
    .addr(address), .data(data_out), .sel(1'b1), .clk(clock), .ld(not_1_out), .clr(reset));
  Multiplexer #(.width(16)) multiplexer_1 (
    .in0(data_in), .in1(undriven), .out(multiplexer_1_out), .sel(not_1_out));  // open: en
  assign data_out = multiplexer_1_out;  // Buffer buffer_1, 16 bits wide
endmodule

module sub_instruction_counter (
  input  new_instruction,
  input  clock,
  input  clear,
  input  lock,
  output [15:0] sub_address
);

  wire [15:0] adder_1_out, multiplexer_1_out, multiplexer_2_out, register_1_q;

  Multiplexer #(.width(16), .enable("false")) multiplexer_1 (
    .in0(adder_1_out), .in1(16'h1), .out(multiplexer_1_out), .sel(new_instruction));
  Multiplexer #(.width(16), .enable("false")) multiplexer_2 (
    .in0(multiplexer_1_out), .in1({16{1'b0}}), .out(multiplexer_2_out), .sel(lock));
  Register #(.width(16)) register_1 (.D(multiplexer_2_out), .Q(register_1_q), .clk(clock), .clr(clear));  // open: en
  Adder #(.width(16)) adder_1 (.a(register_1_q), .b(16'h1), .out(adder_1_out));  // open: cin, cout
  Subtractor #(.width(16)) subtractor_1 (.a(multiplexer_2_out), .b(16'h1), .out(sub_address));  // open: bin, bout
endmodule

// ALU
module alu (
  input  [15:0] in_1,
  input  value_1,
  input  value_2,
  input  clock,
  input  reset,
  output [15:0] out_6,
  output LEQ_zero
);

  wire leq_zero_1_out_2, register_3_q;
  wire [15:0] multiplexer_1_out, multiplexer_2_out, register_1_q, register_2_q;

  Multiplexer #(.width(16), .enable("false")) multiplexer_1 (
    .in0(register_1_q), .in1(in_1), .out(multiplexer_1_out), .sel(value_1));
  Multiplexer #(.width(16), .enable("false")) multiplexer_2 (
    .in0(register_2_q), .in1(in_1), .out(multiplexer_2_out), .sel(value_2));
  Register #(.width(16)) register_1 (.D(multiplexer_1_out), .Q(register_1_q), .clk(clock), .clr(reset));  // open: en
  Register #(.width(16)) register_2 (.D(multiplexer_2_out), .Q(register_2_q), .clk(clock), .clr(reset));  // open: en
  Subtractor #(.width(16)) subtractor_1 (.a(register_1_q), .b(register_2_q), .out(out_6));  // open: bin, bout
  LEQ_zero leq_zero_1 (.in_1(out_6), .out_2(leq_zero_1_out_2));
  Register #(.width(1)) register_3 (.D(leq_zero_1_out_2), .Q(register_3_q), .clk(clock), .clr(reset));  // open: en
  Register #(.width(1)) register_4 (.D(register_3_q), .Q(LEQ_zero), .clk(clock), .clr(reset));  // open: en
endmodule

// DECODER
module decoder (
  input  [15:0] data,
  input  [15:0] sub_instruction,
  input  clock,
  input  reset,
  output [15:0] out_5,
  output [1:0] mem_addr,
  output save_result,
  output value_1,
  output value_2
);

  wire comparator_1_eq, comparator_2_eq, comparator_3_eq, comparator_6_eq;
  wire [15:0] and_1_out, and_2_out, and_3_out, and_4_out, and_5_out, and_6_out, Jump_to_reg_q,
       multiplexer_1_out, multiplexer_2_out, multiplexer_3_out, n1_to_16_bit_1_out_2, n1_to_16_bit_2_out_2,
       n1_to_16_bit_3_out_2, n1_to_16_bit_4_out_2, n1_to_16_bit_5_out_2, n1_to_16_bit_6_out_2, Val_1_q,
       Val_2_q;

  Comparator #(.width(16)) comparator_1 (.a({16{1'b0}}), .b(sub_instruction), .eq(comparator_1_eq));  // open: gt, lt
  Comparator #(.width(16)) comparator_2 (.a(16'h1), .b(sub_instruction), .eq(comparator_2_eq));  // open: gt, lt
  Comparator #(.width(16)) comparator_3 (
    .a(16'h2), .b(sub_instruction), .eq(comparator_3_eq), .lt(mem_addr[0]));  // open: gt
  _1_to_16_bit u_1_to_16_bit_1 (.in_1(comparator_1_eq), .out_2(n1_to_16_bit_1_out_2));
  _1_to_16_bit u_1_to_16_bit_2 (.in_1(comparator_2_eq), .out_2(n1_to_16_bit_2_out_2));
  _1_to_16_bit u_1_to_16_bit_3 (.in_1(comparator_3_eq), .out_2(n1_to_16_bit_3_out_2));
  assign and_1_out = data & n1_to_16_bit_1_out_2;  // AND_Gate and_1, 16 bits wide
  assign and_2_out = data & n1_to_16_bit_2_out_2;  // AND_Gate and_2, 16 bits wide
  assign and_3_out = data & n1_to_16_bit_3_out_2;  // AND_Gate and_3, 16 bits wide
  Multiplexer #(.width(16), .enable("false")) multiplexer_1 (
    .in0(Val_1_q), .in1(and_1_out), .out(multiplexer_1_out), .sel(comparator_1_eq));
  Multiplexer #(.width(16), .enable("false")) multiplexer_2 (
    .in0(Val_2_q), .in1(and_2_out), .out(multiplexer_2_out), .sel(comparator_2_eq));
  Multiplexer #(.width(16), .enable("false")) multiplexer_3 (
    .in0(Jump_to_reg_q), .in1(and_3_out), .out(multiplexer_3_out), .sel(comparator_3_eq));
  Register #(.width(16)) Val_1 (.D(multiplexer_1_out), .Q(Val_1_q), .clk(clock), .clr(reset));  // open: en
  Register #(.width(16)) Val_2 (.D(multiplexer_2_out), .Q(Val_2_q), .clk(clock), .clr(reset));  // open: en
  Register #(.width(16)) Jump_to_reg (.D(multiplexer_3_out), .Q(Jump_to_reg_q), .clk(clock), .clr(reset));  // open: en
  Comparator #(.width(16)) comparator_4 (.a(16'h3), .b(sub_instruction), .eq(value_1));  // open: gt, lt
  Comparator #(.width(16)) comparator_5 (.a(16'h4), .b(sub_instruction), .eq(value_2));  // open: gt, lt
  Comparator #(.width(16)) comparator_6 (.a(16'h7), .b(sub_instruction), .eq(comparator_6_eq));  // open: gt, lt
  Comparator #(.width(16)) comparator_7 (.a(16'h5), .b(sub_instruction), .lt(mem_addr[1]));  // open: gt, eq
  Comparator #(.width(16)) comparator_8 (.a(16'h6), .b(sub_instruction), .eq(save_result));  // open: gt, lt
  _1_to_16_bit u_1_to_16_bit_4 (.in_1(value_1), .out_2(n1_to_16_bit_4_out_2));
  _1_to_16_bit u_1_to_16_bit_5 (.in_1(value_2), .out_2(n1_to_16_bit_5_out_2));
  _1_to_16_bit u_1_to_16_bit_6 (.in_1(comparator_6_eq), .out_2(n1_to_16_bit_6_out_2));
  assign and_4_out = Val_1_q & n1_to_16_bit_4_out_2;  // AND_Gate and_4, 16 bits wide
  assign and_5_out = Val_2_q & n1_to_16_bit_5_out_2;  // AND_Gate and_5, 16 bits wide
  assign and_6_out = Jump_to_reg_q & n1_to_16_bit_6_out_2;  // AND_Gate and_6, 16 bits wide
  assign out_5 = and_4_out | and_5_out | and_6_out;  // OR_Gate or_1, 16 bits wide
endmodule

module _1_to_16_bit (
  input  in_1,
  output [15:0] out_2
);


  assign out_2 = {16{in_1}};
endmodule

module LEQ_zero (
  input  [15:0] in_1,
  output out_2
);

  wire comparator_1_eq;

  Comparator #(.width(16)) comparator_1 (.a({16{1'b0}}), .b(in_1), .eq(comparator_1_eq));  // open: gt, lt
  or or_1 (out_2, comparator_1_eq, in_1[15]);
endmodule

// ROM
module bootloader (
  input  clock,
  input  reset,
  output [15:0] Address,
  output [15:0] Data,
  output Write_ram,
  output unlock_system
);

  wire and_1_out, comparator_1_eq, comparator_1_lt, comparator_2_eq, comparator_2_lt, not_1_out, not_2_out,
       or_1_out;
  wire [15:0] counter_1_q, multiplexer_1_out, register_1_q;

  and and_1 (and_1_out, 1'b1, not_1_out);
  Counter #(.width(16), .max('hffff)) counter_1 (
    .load(1'b0), .count(and_1_out), .Q(counter_1_q), .clk(clock));  // open: D, carry, clr
  not not_1 (not_1_out, unlock_system);
  Multiplexer #(.width(16), .enable("false")) multiplexer_1 (
    .in0(Data), .in1(register_1_q), .out(multiplexer_1_out), .sel(comparator_2_lt));
  ROM #(.addrWidth(16), .dataWidth(16)) rom_1 (.addr(counter_1_q), .data(Data), .sel(not_1_out));
  Register #(.width(16)) register_1 (.D(multiplexer_1_out), .Q(register_1_q), .clk(clock), .clr(reset));  // open: en
  Comparator #(.width(16)) comparator_1 (
    .a(counter_1_q), .b(register_1_q), .gt(unlock_system), .eq(comparator_1_eq), .lt(comparator_1_lt));
  Comparator #(.width(16)) comparator_2 (
    .a({16{1'b0}}), .b(register_1_q), .eq(comparator_2_eq), .lt(comparator_2_lt));  // open: gt
  or or_1 (or_1_out, comparator_1_eq, comparator_1_lt);
  not not_2 (not_2_out, comparator_2_eq);
  Subtractor #(.width(16)) subtractor_1 (.a(counter_1_q), .b(16'h1), .out(Address));  // open: bin, bout
  and and_2 (Write_ram, not_2_out, or_1_out);

  // Notes on the sheet:
  //   contents of rom_1 (hex, n*v repeats v):
  //   9 3 4 6 7 1 4 3 4
endmodule
